// Digital circuit RIA.dig as structural Verilog
module RIA (
  input  [15:0] ADDR,
  input  RWB,
  input  PHI2,
  input  IRQB_2,
  input  nIRQ,
  output WE,
  output IRQB
);

  wire CE, CS0, nand_1_out, nand_3_out, nand_4_out, nand_5_out, not_1_out, RAM_out, RIA_out, VIA_out;

  nand nand_1 (nand_1_out, ADDR[8], ADDR[9], ADDR[10], ADDR[11], ADDR[12], ADDR[13], ADDR[14], ADDR[15]);
  nand nand_2 (WE, PHI2, not_1_out);
  not not_1 (not_1_out, RWB);
  nand nand_3 (nand_3_out, IRQB_2, nIRQ);
  nand nand_4 (nand_4_out, ADDR[5], ADDR[6]);
  nand nand_5 (nand_5_out, ADDR[7], CE);
  not not_2 (CE, nand_1_out);
  nor nor_1 (CS0, nand_4_out, nand_5_out);
  not not_3 (IRQB, nand_3_out);
  LookUpTable RIA (.in0(CS0), .in1(1'b0), .out(RIA_out));
  LookUpTable VIA (.in0(CE), .in1(CS0), .out(VIA_out));
  LookUpTable RAM (.in0(CE), .in1(CE), .out(RAM_out));
  LED led_1 (.in(RIA_out));
  LED led_2 (.in(VIA_out));
  LED led_3 (.in(RAM_out));

  // Other names for the same wires on the sheet: A0 = ADDR[0]; A1 = ADDR[1]; A2 = ADDR[2]; A3 = ADDR[3]; A4 = ADDR[4];
  //   A5 = ADDR[5]; A6 = ADDR[6]; A7 = ADDR[7]; A8 = ADDR[8]; A9 = ADDR[9]; A10 = ADDR[10]; A11 = ADDR[11];
  //   A12 = ADDR[12]; A13 = ADDR[13]; A14 = ADDR[14]; A15 = ADDR[15]; CS2B = CS0; CS1 = CE; OE = CE

  // Notes on the sheet:
  //   ADDR: default 65260
  //   RWB: default 1
  //   PHI2: default 1
  //   IRQB_2: default 1
  //   nIRQ: default 1
  //   7430
  //   contents of RIA (hex, n*v repeats v):
  //   0,1
  //   contents of VIA (hex, n*v repeats v):
  //   0,1
  //   contents of RAM (hex, n*v repeats v):
  //   1
  //   Decode Test
endmodule
